# Fritzing sketch sketch (saved by Fritzing 0.9.3b)
breadboards: 1

parts:
  PIR1 = PIR sensor
  R1 = Resistor [tolerance=±5% resistance=220 package=THT]
  Raspberry_Pi = Raspberry Pi B+
  CAMERA1 = TTL Serial JPEG Camera  # not connected

nets:
  N1: PIR1.VDD, R1.Pin_0
  N2: PIR1.SIG, Raspberry_Pi.GPIO18
  GND: PIR1.GND, Raspberry_Pi.GND
  N3: R1.Pin_1, Raspberry_Pi.5V

notes:
  Didn't find a raspberry pi camera V2 in the "parts" this is the only camera
  In the project the camera is connected to the15pin MIPI CSI
  CSI here

custom parts:
  TTL Serial JPEG Camera: TTL Serial JPEG Camera with NTSC Out
